# Fritzing sketch robot-arduino-lego-d (saved by Fritzing 0.9.3b)
breadboards: 2

parts:
  Part3 = Arduino Uno (Rev3)
  R1 = Resistor [tolerance=±5% resistance=22k package="0603 [SMD]"]
  R2 = Resistor [tolerance=±5% resistance=22k package="0603 [SMD]"]

nets:
  N1: Part3.A0, R2.Pin_0
  N2: Part3.A1, R1.Pin_1
  N3: Part3.5V, R1.Pin_0, R2.Pin_1

notes:
  This extra breadboard represents the extra headers for 5V and GND on the s specific prototyping shields I am using.
  RN42 GND
  RN42 Vin
  RN42 Reset (Unused)
  RN42 Rx
  RN42 Tx
  RN42 RTS
  RN42 CTS
  Proto Shield GND Header (5 pins)
  Proto Shield 5V Header (5 pins)
  RN42 Pins
  MotorShield I2C SCL
  MotorShield I2C SDA
  LEGO Rotation Left
  LEGO Rotation Right
  Sonar Echo
  Sonar Trig
  Hardware Interrupt (Available)
  Motorshield Servo 1
  Motorshield Servo 2
  RS
  Neopixel
  This layout will allow the Arduino to control:
  1) Motorshield
  2) LEGO Rotation x2
  3) Servo Motor x2
  4) Ultrasonic Sensor
  5) NeoPixel Ring
  6) PixeyCam
  Sonar Pins
